// Logisim project base.circ as structural Verilog: 1 circuit, main circuit Teste
module Teste (
  input  in_1,
  output Jc,
  output Jb,
  output Kb,
  output Ja,
  output Ka,
  output out_7,
  output out_8,
  output out_9
);

  wire clock_1_out, not_1_out, not_2_out;

  not not_1 (not_1_out, out_8);
  or or_1 (Kb, Jb, out_7);
  not not_2 (not_2_out, out_7);
  or or_2 (Ka, out_8, out_7);
  or or_3 (Jc, not_1_out, Jb);
  or or_4 (Ja, not_2_out, out_8);
  Clock clock_1 (.out(clock_1_out));
  J_K_Flip_Flop j_k_ff_1 (.J(Jc), .clk(clock_1_out), .K(1'b1), .Q(out_7), .reset(in_1));  // open: Qn, preset, en
  J_K_Flip_Flop j_k_ff_2 (.J(Jb), .clk(clock_1_out), .K(Kb), .Q(out_8), .reset(in_1));  // open: Qn, preset, en
  J_K_Flip_Flop j_k_ff_3 (.J(Ja), .clk(clock_1_out), .K(Ka), .Q(Jb), .reset(in_1));  // open: Qn, preset, en

  assign out_9 = Jb;

  // Notes on the sheet:
  //   C
  //   B
  //   A
endmodule
